# Fritzing sketch Schematics (saved by Fritzing 0.9.3b)
breadboards: 1

parts:
  Part1 = Arduino Uno (Rev3)
  S1 = Pushbutton [package="[THT]"]
  S2 = Pushbutton [package="[THT]"]
  S3 = Pushbutton [package="[THT]"]
  R1 = Resistor [tolerance=±5% resistance=10k package=THT]
  R2 = Resistor [tolerance=±5% resistance=10k package=THT]
  R3 = Resistor [tolerance=±5% resistance=10k package=THT]  # not connected
  HC-SR04_Sensor_1 = HC-SR04 Ultrasonic Distance Sensor
  Grove1 = Grove 3 Axis Digital Accelerometer 16g

nets:
  N1: Part1.D9_PWM, HC-SR04_Sensor_1.TRIG
  N2: Part1.D10_PWM/SS, HC-SR04_Sensor_1.ECHO
  N3: Part1.A4/SDA, Grove1.SDA
  N4: Part1.A5/SCL, Grove1.SCL
  N5: Part1.D2, S1.Pin_1, S1.Pin_2
  N6: Part1.D3_PWM, S2.Pin_1, S2.Pin_2, R2.Pin_0
  N7: Part1.D4, S3.Pin_1, S3.Pin_2, R1.Pin_0
  VCC: Part1.5V, S1.Pin_3, S1.Pin_4, S2.Pin_3, S2.Pin_4, S3.Pin_3, S3.Pin_4, HC-SR04_Sensor_1.VCC, Grove1.VCC
  GND: Part1.GND, R1.Pin_1, R2.Pin_1, HC-SR04_Sensor_1.GND, Grove1.GND
